// Logisim project ex1.circ as structural Verilog: 1 circuit, main circuit generate_immediate
module generate_immediate (
  input  [31:0] INSTRUCTION,
  output [31:0] IMMEDIATE
);

  wire [31:0] bit_extender_1_out, bit_extender_2_out, shifter_1_out;

  assign bit_extender_1_out = {{27{1'b0}}, INSTRUCTION[11:7]};  // Bit_Extender bit_extender_1
  assign bit_extender_2_out = {{25{INSTRUCTION[31]}}, INSTRUCTION[31:25]};  // Bit_Extender bit_extender_2
  Shifter #(.width(32)) shifter_1 (.in(bit_extender_2_out), .\dist (5'b00101), .out(shifter_1_out));
  Adder #(.width(32)) adder_1 (.a(bit_extender_1_out), .b(shifter_1_out), .out(IMMEDIATE));  // open: cin, cout
endmodule
