// Logisim project ex2.circ as structural Verilog: 1 circuit, main circuit compute_BrUn
module compute_BrUn (
  input  [31:0] INSTRUCTION,
  output BrUn
);

  wire and_1_out, bit_extender_1_out;
  wire [6:0] not_1_out, xor_1_out;

  assign xor_1_out = 7'b1100011 ^ INSTRUCTION[6:0];  // XOR_Gate xor_1, 7 bits wide
  and and_1 (and_1_out, INSTRUCTION[13], INSTRUCTION[14]);
  Bit_Extender #(.in_width(7), .out_width(1)) bit_extender_1 (.in(not_1_out), .out(bit_extender_1_out));
  assign not_1_out = ~xor_1_out;  // NOT_Gate not_1, 7 bits wide
  and and_2 (BrUn, bit_extender_1_out, and_1_out);
endmodule
